# Fritzing sketch ElectronWeatherProtoboard (saved by Fritzing 0.9.3b)
perfboards: 1

parts:
  S4 = Reed switch [package=THT]
  Part1 = Electron
  R5 = PHOTOCELL [package=photocell]
  R6 = Resistor [tolerance=±5% resistance=220 package="1206 [SMD]"]
  R7 = Resistor [tolerance=±5% resistance=220 package="1206 [SMD]"]
  R9 = Resistor [tolerance=±5% resistance=220 package="1206 [SMD]"]
  RHT1 = Humidity and Temperature Sensor RHT03
  JP1 = Header 8 [package=1x08_smd]
  Part2 = Soil Moisture Sensor

nets:
  3V3: S4.pin_1, Part1.3V3, R9.Pin_1, RHT1.GND_2, JP1.8, Part2.VCC
  N1: S4.pin_2, Part1.D2, R7.Pin_0
  N2: Part1.A0, R5.P$2, R6.Pin_0
  N3: Part1.D0, JP1.5
  N4: Part1.D1, JP1.6
  N5: Part1.D7, R6.Pin_1, R7.Pin_1, RHT1.Vcc
  N6: R9.Pin_0, RHT1.GND_1
  N7: JP1.1, Part2.SIG
  N8: JP1.4, JP1.7
