# Fritzing sketch ElectronWeather_Protoboard (saved by Fritzing 0.9.3b)
perfboards: 1

parts:
  S4 = Reed switch [package=THT]
  Part1 = Electron
  R5 = PHOTOCELL [package=photocell]
  R6 = Resistor [tolerance=±5% resistance=220 package="1206 [SMD]"]
  R7 = Resistor [tolerance=±5% resistance=220 package="1206 [SMD]"]  # not connected
  R9 = Resistor [tolerance=±5% resistance=220 package="1206 [SMD]"]
  RHT1 = Humidity and Temperature Sensor RHT03
  JP1 = Header 8 [package=1x08_smd]
  Part2 = Soil Moisture Sensor
  U1 = HALL-EFFECT [package=sc70]  # not connected

nets:
  N1: S4.pin_2, Part1.D2
  N2: Part1.A1, R5.P$2, R6.Pin_0
  N3: Part1.D0, JP1.5
  N4: Part1.D1, JP1.6
  N5: Part1.D5, R9.Pin_0, RHT1.Data-signal, RHT1.GND_1
  3V3: Part1.3V3, RHT1.Vcc
  N6: JP1.1, Part2.SIG

notes:
  Anemometer (12V) --> A2
  Photoresistor --> A1
  Temp/Humidity --> D5
  Watermark --> ADS1115 A3 pin
  Reed Switch --> D2
  ADS1115 16-bit Converter --> SCL to D1 (green), SDA to D0 (grey)
  12V --> VIN
