# Fritzing sketch ElectronWeather_Protoboard2 (saved by Fritzing 0.9.3b)
perfboards: 1

parts:
  S4 = Reed switch [package=THT]
  Part1 = Electron
  R5 = PHOTOCELL [package=photocell]
  R6 = Resistor [tolerance=±5% resistance=220 package="1206 [SMD]"]
  R7 = Resistor [tolerance=±5% resistance=220 package="1206 [SMD]"]  # not connected
  R9 = Resistor [tolerance=±5% resistance=220 package="1206 [SMD]"]
  RHT1 = Humidity and Temperature Sensor RHT03
  JP1 = Header 8 [package=1x08_smd]
  Part2 = Soil Moisture Sensor
  U1 = HALL-EFFECT [package=sc70]  # not connected
  J1 = Camdenboss CTB0158-4 [part_number=CTB0158-4 package=THT]
  J2 = Camdenboss CTB0158-4 [part_number=CTB0158-4 package=THT]
  J3 = Camdenboss CTB0158-4 [part_number=CTB0158-4 package=THT]
  J4 = Camdenboss CTB0158-4 [part_number=CTB0158-4 package=THT]  # not connected
  J5 = Camdenboss CTB0158-4 [part_number=CTB0158-4 package=THT]
  J6 = Camdenboss CTB0158-4 [part_number=CTB0158-4 package=THT]
  R10 = Resistor [tolerance=±5% resistance=220 package="1206 [SMD]"]
  R11 = Resistor [tolerance=±5% resistance=220 package="1206 [SMD]"]
  R12 = Resistor [tolerance=±5% resistance=220 package="1206 [SMD]"]
  Part3 = Electron
  JP2 = Header 8 [package=1x08_smd]

nets:
  N1: S4.pin_2, Part1.D2
  N2: Part1.A1, R5.P$2, R6.Pin_0
  N3: Part1.D0, JP1.5
  N4: Part1.D1, JP1.6
  N5: Part1.D5, R9.Pin_0, RHT1.Data-signal, RHT1.GND_1
  3V3: Part1.3V3, RHT1.Vcc
  N6: JP1.1, Part2.SIG
  N7: J1.pin4, JP2.1
  N8: J2.pin1, Part3.D5
  N9: J2.pin2, Part3.D2
  N10: J3.pin1, R12.Pin_1
  N11: J3.pin4, R10.Pin_0, Part3.GND
  N12: J5.pin2, R11.Pin_1, Part3.A1
  N13: J5.pin3, Part3.A2
  N14: J6.pin3, R11.Pin_0, Part3.VIN
  N15: Part3.D0, JP2.5
  N16: Part3.D1, JP2.6
  N17: JP2.4, JP2.7

notes:
  Anemometer (12V) --> A2
  Photoresistor --> A1
  Temp/Humidity --> D5
  Watermark --> ADS1115 A3 pin
  Reed Switch --> D2
  ADS1115 16-bit Converter --> SCL to D1 (green), SDA to D0 (grey)
  12V --> VIN
  Y - photoresistor
  Blu - anemometer
  Bla - 10K ohm
  Bla - ground
  R - 12v in
  R - 3v3 out
  W - reed switch
  W res - 200 ohm
  Green - temp/humidity
  Green res - 10k ohm
  Black bar is ADS1115 16-bit converter
  Grey - ADS1115 SDA (D0)
  P - ADS1115 SCL (D1)
  Bla - ground
  R - 3v3
  Cyan - watermark
