# Fritzing sketch ElectronWeather_Protoboard3 (saved by Fritzing 0.9.3b)
perfboards: 1

parts:
  S4 = Reed switch [package=THT]
  Part1 = Electron
  R5 = PHOTOCELL [package=photocell]
  R6 = Resistor [tolerance=±5% resistance=220 package="1206 [SMD]"]
  R7 = Resistor [tolerance=±5% resistance=220 package="1206 [SMD]"]  # not connected
  R9 = Resistor [tolerance=±5% resistance=220 package="1206 [SMD]"]
  RHT1 = Humidity and Temperature Sensor RHT03
  JP1 = Header 8 [package=1x08_smd]
  Part2 = Soil Moisture Sensor
  U1 = HALL-EFFECT [package=sc70]  # not connected
  J2 = Camdenboss CTB0158-4 [part_number=CTB0158-4 package=THT]
  J3 = Camdenboss CTB0158-4 [part_number=CTB0158-4 package=THT]
  J5 = Camdenboss CTB0158-4 [part_number=CTB0158-4 package=THT]
  J6 = Camdenboss CTB0158-4 [part_number=CTB0158-4 package=THT]
  R10 = Resistor [tolerance=±5% resistance=220 package="1206 [SMD]"]
  R11 = Resistor [tolerance=±5% resistance=220 package="1206 [SMD]"]
  R12 = Resistor [tolerance=±5% resistance=220 package="1206 [SMD]"]
  Part3 = Electron
  JP2 = Header 8 [package=1x08_smd]
  R13 = Resistor [tolerance=±5% resistance=220 package="1206 [SMD]"]
  J7 = Camdenboss CTB0158-5 [part_number=CTB0158-5 package=THT]

nets:
  N1: S4.pin_2, Part1.D2
  N2: Part1.A1, R5.P$2, R6.Pin_0
  N3: Part1.D0, JP1.5
  N4: Part1.D1, JP1.6
  N5: Part1.D5, R9.Pin_0, RHT1.Data-signal, RHT1.GND_1
  3V3: Part1.3V3, RHT1.Vcc
  N6: JP1.1, Part2.SIG
  N7: J2.pin1, Part3.D5
  N8: J2.pin2, Part3.D4, R13.Pin_1
  N9: J2.pin3, Part3.D3
  N10: J2.pin4, Part3.D2
  N11: J3.pin1, R12.Pin_1
  N12: J3.pin3, R10.Pin_0
  N13: J3.pin4, Part3.GND, JP2.4, JP2.7
  N14: J5.pin1, R11.Pin_1, Part3.A1
  N15: J5.pin2, Part3.A2
  N16: J5.pin3, Part3.A3
  N17: J5.pin4, Part3.A4
  N18: J6.pin1, Part3.RX
  N19: J6.pin2, Part3.TX
  N20: J6.pin3, R11.Pin_0, Part3.VIN
  N21: Part3.D0, JP2.5, J7.pin2
  N22: Part3.D1, JP2.6, J7.pin1
  N23: Part3.C0, J7.pin5
  N24: Part3.C1, J7.pin4
  N25: JP2.1, J7.pin3

notes:
  Anemometer (12V) --> A2
  Photoresistor --> A1
  Temp/Humidity --> D5
  Watermark --> ADS1115 A3 pin
  Reed Switch --> D2
  ADS1115 16-bit Converter --> SCL to D1 (green), SDA to D0 (grey)
  12V --> VIN
  Y: A1 - photoresistor
  Y:A1 - 10K ohm
  Blu: A2 - anemometer
  Brown: A3 - open
  Pink: A4 - open
  Bla - ground
  R - 12v in
  Y:RX - open
  Green: TX - open
  R - 3v3 out
  Bla - ground
  W - reed switch
  W res - 200 ohm
  Pink: D3 - open
  Orange - soil temp
  Orange res - 4.7k ohm
  Green - temp/humidity
  Green res - 10k ohm
  Black bar is ADS1115 16-bit converter
  Grey: D0 - ADS1115 SDA
  Blue: D1 - ADS1115 SCL
  Bla - ground
  R - 3v3
  *Have female headers so ADS1115 can just be plugged into board
  Pink: C0 - SD card writer
  Green: C1 - SD card writer
  Cyan: ADS1115 A3 - watermark
  Grey: D0 - ADS1115 SDA
  Blue: D1 - ADS1115 SCL
  ** Check: can lux sensor go directly to D0/D1 while ADS1115 is also connected to D0/D1?
