# Fritzing sketch ElectronWeather_Protoboard4 (saved by Fritzing 0.9.3b)

parts:
  J2 = Camdenboss CTB0158-4 [part_number=CTB0158-4 package=THT]
  J3 = Camdenboss CTB0158-4 [part_number=CTB0158-4 package=THT]
  J5 = Camdenboss CTB0158-4 [part_number=CTB0158-4 package=THT]
  J6 = Camdenboss CTB0158-4 [part_number=CTB0158-4 package=THT]
  R10 = Resistor [tolerance=±5% resistance=220 package="1206 [SMD]"]
  R11 = Resistor [tolerance=±5% resistance=220 package="1206 [SMD]"]
  R12 = Resistor [tolerance=±5% resistance=220 package="1206 [SMD]"]
  Part3 = Electron
  R13 = Resistor [tolerance=±5% resistance=220 package="1206 [SMD]"]
  J9 = Camdenboss CTB0158-4 [part_number=CTB0158-4 package=THT]
  J10 = Camdenboss CTB0158-4 [part_number=CTB0158-4 package=THT]
  R14 = Resistor [tolerance=±5% resistance=220 package="1206 [SMD]"]  # not connected

nets:
  N1: J2.pin1, Part3.D5
  N2: J2.pin2, Part3.D4, R13.Pin_1
  N3: J2.pin3, Part3.D3
  N4: J2.pin4, Part3.D2
  N5: J3.pin1, R12.Pin_1, Part3.3V3
  N6: J3.pin3, R10.Pin_0
  N7: J3.pin4, J6.pin3, R11.Pin_0, Part3.GND
  N8: J5.pin1, R11.Pin_1, Part3.A1
  N9: J5.pin2, Part3.A2
  N10: J5.pin3, Part3.A3
  N11: J5.pin4, Part3.A4
  N12: J6.pin1, Part3.RX
  N13: J6.pin2, Part3.TX
  N14: J6.pin4, Part3.VIN
  N15: Part3.A0, J10.pin4
  N16: Part3.C0, J9.pin4
  N17: Part3.C1, J9.pin3
  N18: Part3.C4, J9.pin2
  N19: Part3.C5, J9.pin1

notes:
  Y: A1 - photoresistor
  Y:A1 - 10K ohm
  Blu: A2 - anemometer
  Orange: A3 - Watermark analog voltage adapter
  Pink: A4 - Li-Cor solar radiation
  Bla - ground
  R - 12v in
  Y:RX - open
  Green: TX - open
  R - 3v3 out
  Bla - ground
  W - reed switch
  W res - 200 ohm
  Pink: D3 - open
  Orange - soil temp
  Orange res - 4.7k ohm
  Green - temp/humidity
  Green res - 10k ohm
  Pink: C0 - to Tx on SD card writer
  Green: C1 - to Rx on SD card writer
  Grey: C4 - TSL2591 lux SDA
  Blue: C5 - TSL2591 lux SCL
  The open log should be a header and not a screw terminal
